// Logisim project MEALY MACHINE_13456938_Lonergan.circ as structural Verilog: 1 circuit, main circuit main
module main (
  input  X,
  output Z1,
  output Z0
);

  wire and_1_out, and_2_out, and_3_out, and_4_out, and_5_out, clock_1_out, j_k_ff_1_q, j_k_ff_2_q,
       j_k_ff_3_q, not_1_out, not_2_out, not_3_out, not_4_out, or_1_out, or_2_out, or_3_out;

  not not_1 (not_1_out, X);
  not not_2 (not_2_out, j_k_ff_1_q);
  not not_3 (not_3_out, j_k_ff_1_q);
  not not_4 (not_4_out, j_k_ff_3_q);
  and and_1 (and_1_out, j_k_ff_3_q, X);
  and and_2 (and_2_out, j_k_ff_1_q, not_1_out);
  and and_3 (and_3_out, not_3_out, and_1_out);
  and and_4 (and_4_out, not_4_out, not_1_out);
  or or_1 (or_1_out, X, not_3_out);
  Clock clock_1 (.out(clock_1_out));
  and and_5 (and_5_out, not_2_out, and_1_out);
  or or_2 (or_2_out, and_3_out, and_4_out);
  or or_3 (or_3_out, and_5_out, and_2_out);
  J_K_Flip_Flop j_k_ff_1 (
    .J(and_1_out), .clk(clock_1_out), .K(not_1_out), .Q(j_k_ff_1_q));  // open: Qn, preset, en, reset
  J_K_Flip_Flop j_k_ff_2 (
    .J(or_3_out), .clk(clock_1_out), .K(or_2_out), .Q(j_k_ff_2_q));  // open: Qn, preset, en, reset
  J_K_Flip_Flop j_k_ff_3 (.J(X), .clk(clock_1_out), .K(or_1_out), .Q(j_k_ff_3_q));  // open: Qn, preset, en, reset
  and and_6 (Z1, j_k_ff_1_q, X, j_k_ff_3_q);
  and and_7 (Z0, j_k_ff_2_q, X, j_k_ff_3_q);

  // Notes on the sheet:
  //   X'
  //   Q2'
  //   Q0.X
  //   Q2.X'
  //   Q2'.Q0.X
  //   Q0'.X'
  //   Q2'+X
  //   CLK
  //   Q2'Q0X
  //   Q2'Q0.X+Q2'.X'
  //   Q0'.X'+Q2'.Q0.X
  //   JK 2
  //   JK1
  //   JK0
  //   Q2
  //   Q1
  //   Q0
endmodule
