// Logisim project MOORE MACHINE_13456938_Lonergan.circ as structural Verilog: 1 circuit, main circuit main
module main (
  input  X,
  output Q2Q1Q0,
  output out_3
);

  wire and_1_out, and_2_out, and_3_out, and_4_out, and_5_out, and_6_out, and_7_out, and_8_out, and_9_out,
       clock_1_out, j_k_ff_1_q, j_k_ff_2_q, j_k_ff_3_q, not_1_out, not_2_out, not_3_out, not_4_out,
       not_5_out, not_6_out, not_7_out, not_8_out, or_1_out, or_2_out, or_3_out, or_4_out, or_5_out;

  not not_1 (not_1_out, X);
  not not_2 (not_2_out, X);
  not not_3 (not_3_out, j_k_ff_2_q);
  and and_1 (and_1_out, j_k_ff_2_q, j_k_ff_3_q);
  and and_2 (and_2_out, j_k_ff_1_q, not_2_out, not_3_out);
  and and_3 (and_3_out, not_2_out, j_k_ff_3_q);
  not not_4 (not_4_out, j_k_ff_1_q);
  not not_5 (not_5_out, j_k_ff_3_q);
  and and_4 (and_4_out, j_k_ff_1_q, j_k_ff_2_q, not_1_out);
  and and_5 (and_5_out, j_k_ff_3_q, X);
  or or_1 (or_1_out, and_1_out, and_2_out);
  or or_2 (or_2_out, j_k_ff_1_q, and_3_out);
  and and_6 (and_6_out, and_3_out, not_4_out);
  and and_7 (and_7_out, not_4_out, not_2_out, not_5_out);
  and and_8 (and_8_out, not_4_out, j_k_ff_3_q, X);
  not not_6 (not_6_out, j_k_ff_1_q);
  or or_3 (or_3_out, and_6_out, and_7_out, and_8_out);
  and and_9 (and_9_out, X, not_6_out);
  or or_4 (or_4_out, and_9_out, and_4_out);
  or or_5 (or_5_out, j_k_ff_2_q, not_1_out);
  Clock clock_1 (.out(clock_1_out));
  J_K_Flip_Flop j_k_ff_1 (
    .J(and_5_out), .clk(clock_1_out), .K(or_1_out), .Q(j_k_ff_1_q));  // open: Qn, preset, en, reset
  J_K_Flip_Flop j_k_ff_2 (
    .J(or_2_out), .clk(clock_1_out), .K(or_3_out), .Q(j_k_ff_2_q));  // open: Qn, preset, en, reset
  J_K_Flip_Flop j_k_ff_3 (
    .J(or_4_out), .clk(clock_1_out), .K(or_5_out), .Q(j_k_ff_3_q));  // open: Qn, preset, en, reset
  not not_7 (not_7_out, j_k_ff_2_q);
  not not_8 (not_8_out, j_k_ff_3_q);
  and and_10 (Q2Q1Q0, j_k_ff_1_q, j_k_ff_2_q, j_k_ff_3_q);
  and and_11 (out_3, j_k_ff_1_q, not_7_out, not_8_out);

  // Notes on the sheet:
  //   X'
  //   Q1.Q0
  //   Q2.Q1'.X'
  //   Q0.X'
  //   Q0.X' Q2'
  //   Q2Q1X'
  //   Q0.X
  //   Q2.Q1'.X'+Q1.Q0
  //   Q0.X'+ Q2
  //   Q0'.X'.Q2'
  //   Q0.X.Q2'
  //   Q0.X' Q2+Q2'Q0'X'+Q2'Q0X'
  //   Q2'X
  //   Q2'X+Q2Q1X'
  //   Q1+X'
  //   Q2
  //   Q1
  //   Q0
  //   Q2Q1'Q0'
endmodule
