// Logisim project RS-Latch.circ as structural Verilog: 5 circuits, main circuit RS-Latch
module RS_Latch (
  input  R,
  input  S,
  output Q,
  output Q_prime
);

  nor nor_1 (Q, R, Q_prime);
  nor nor_2 (Q_prime, Q, S);
endmodule

module RS_Latch_with_Enable (
  input  R,
  input  ENABLE,
  input  S,
  output Q,
  output Q_prime
);

  wire and_1_out, and_2_out;

  and and_1 (and_1_out, R, ENABLE);
  and and_2 (and_2_out, ENABLE, S);
  RS_Latch rs_latch_1 (.R(and_1_out), .S(and_2_out), .Q(Q), .Q_prime(Q_prime));
endmodule

module D_Latch (
  input  D,
  input  Enable,
  output Q,
  output Q_prime
);

  wire not_1_out;

  not not_1 (not_1_out, D);
  RS_Latch_with_Enable rs_latch_with_enable_1 (.R(not_1_out), .ENABLE(Enable), .S(D), .Q(Q), .Q_prime(Q_prime));
endmodule

module Master_Slave_D_Type_Flip_Flop (
  input  D,
  output Q,
  output Q_prime
);

  wire CLOCK_out, d_latch_1_q, not_1_out;

  Clock CLOCK (.out(CLOCK_out));
  not not_1 (not_1_out, CLOCK_out);
  D_Latch d_latch_1 (.D(D), .Enable(not_1_out), .Q(d_latch_1_q));  // open: Q_prime
  D_Latch d_latch_2 (.D(d_latch_1_q), .Enable(CLOCK_out), .Q(Q), .Q_prime(Q_prime));
endmodule

module nnnnnnn (
  input  in_1,
  input  in_2,
  output out_3,
  output out_4
);

  RS_Latch rs_latch_1 (.R(in_1), .S(in_2), .Q(out_3), .Q_prime(out_4));
endmodule
